// Logisim project Control Unit.circ as structural Verilog
module Control_Unit (
  input  [2:0] in_1,
  output RegDest,
  output RegWrite,
  output ALUSRC,
  output MemRead,
  output MemWrite,
  output MemToReg,
  output Branch,
  output Jump,
  output [1:0] ALU_OP
);

  wire not_1_out, not_2_out, not_3_out, not_4_out, not_5_out, not_6_out, not_7_out, not_8_out, not_9_out,
       not_10_out;

  not not_1 (not_1_out, in_1[1]);
  not not_2 (not_2_out, in_1[2]);
  and R_Type (ALU_OP[1], not_2_out, not_1_out, not_3_out);
  not not_3 (not_3_out, in_1[0]);
  not not_4 (not_4_out, in_1[2]);
  not not_5 (not_5_out, in_1[2]);
  not not_6 (not_6_out, in_1[1]);
  and Lw (MemRead, not_4_out, not_6_out, in_1[0]);
  not not_7 (not_7_out, in_1[0]);
  and Sw (MemWrite, not_5_out, in_1[1], not_7_out);
  not not_8 (not_8_out, in_1[2]);
  and Beq (ALU_OP[0], not_8_out, in_1[1], in_1[0]);
  not not_9 (not_9_out, in_1[1]);
  and u_Jump (Jump, in_1[2], not_9_out, not_10_out);
  not not_10 (not_10_out, in_1[0]);
  or or_1 (RegWrite, ALU_OP[1], MemRead);
  or or_2 (ALUSRC, MemRead, MemWrite);

  assign Branch = ALU_OP[0];
  assign MemToReg = MemRead;
  assign RegDest = ALU_OP[1];

  // Notes on the sheet:
  //   Control Unit 
endmodule
