// Logisim project Final.circ as structural Verilog: 1 circuit, main circuit main
module main (
  input  in_1,
  output [15:0] out_2,
  output [15:0] out_3,
  output out_4,
  output [1:0] out_5,
  output [3:0] out_6
);

  wire and_1_out, CLK_out, Control_Unit_alusrc, Control_Unit_branch, Control_Unit_jump, Control_Unit_memread,
       Control_Unit_memtoreg, Control_Unit_memwrite, Control_Unit_regdest, Control_Unit_regwrite;
  wire [1:0] Control_Unit_alu_op;
  wire [2:0] multiplexer_1_out;
  wire [15:0] adder_1_out, adder_2_out, bit_extender_1_out, Jump_out_3, multiplexer_2_out, multiplexer_3_out,
       multiplexer_4_out, n16_bit_alu_1_alu_output, n16_bit_register_file_1_read_data_1, PC_q, ram_1_data,
       rom_1_data;

  Register #(.width(16)) PC (.D(multiplexer_4_out), .Q(PC_q), .clk(CLK_out), .clr(1'b0));  // open: en
  Clock CLK (.out(CLK_out));
  Adder #(.width(16)) adder_1 (.a(PC_q), .b(16'h1), .out(adder_1_out), .cin(in_1));  // open: cout
  ROM #(.addrWidth(16), .dataWidth(16)) rom_1 (.addr(PC_q), .data(rom_1_data));  // open: sel
  Control_Unit Control_Unit (
    .in_1(rom_1_data[15:13]), .RegDest(Control_Unit_regdest), .RegWrite(Control_Unit_regwrite),
    .ALUSRC(Control_Unit_alusrc), .MemRead(Control_Unit_memread), .MemWrite(Control_Unit_memwrite),
    .MemToReg(Control_Unit_memtoreg), .Branch(Control_Unit_branch), .Jump(Control_Unit_jump),
    .ALU_OP(Control_Unit_alu_op));
  Jump Jump (.PC(adder_1_out), .Instruction(rom_1_data), .out_3(Jump_out_3));
  Multiplexer #(.width(3), .enable("false")) multiplexer_1 (
    .in0(rom_1_data[9:7]), .in1(rom_1_data[6:4]), .out(multiplexer_1_out), .sel(Control_Unit_regdest));
  _16_Bit_Register_File u_16_bit_register_file_1 (
    .Write_Data(out_2), .Read_Data_1(n16_bit_register_file_1_read_data_1),
    .Read_Register_1(rom_1_data[12:10]), .Read_Data_2(out_3), .Read_Register_2(rom_1_data[9:7]),
    .RegWrite(Control_Unit_regwrite), .CLK(CLK_out), .Write_Register(multiplexer_1_out));
  assign bit_extender_1_out = {{9{rom_1_data[6]}}, rom_1_data[6:0]};  // Bit_Extender bit_extender_1
  Adder #(.width(16)) adder_2 (.a(adder_1_out), .b(bit_extender_1_out), .out(adder_2_out));  // open: cin, cout
  Multiplexer #(.width(16), .enable("false")) multiplexer_2 (
    .in0(out_3), .in1(bit_extender_1_out), .out(multiplexer_2_out), .sel(Control_Unit_alusrc));
  and and_1 (and_1_out, Control_Unit_branch, out_4);
  ALU_Control ALU_OP (.ALU_OP(Control_Unit_alu_op), .Funct_Bits(rom_1_data[3:0]), .ALU_Control_Op({out_6[3:2], out_5}));
  Multiplexer #(.width(16), .enable("false")) multiplexer_3 (
    .in0(adder_1_out), .in1(adder_2_out), .out(multiplexer_3_out), .sel(and_1_out));
  _16_Bit_ALU u_16_bit_alu_1 (
    .A(n16_bit_register_file_1_read_data_1), .B(multiplexer_2_out), .Zero_Flag(out_4),
    .ALU_Output(n16_bit_alu_1_alu_output), .B_Invert(out_6[2]), .ALU_Op(out_5));  // open: Overflow_Flag, C_Out
  Multiplexer #(.width(16), .enable("false")) multiplexer_4 (
    .in0(multiplexer_3_out), .in1(Jump_out_3), .out(multiplexer_4_out), .sel(Control_Unit_jump));
  Multiplexer #(.width(16), .enable("false")) multiplexer_5 (
    .in0(n16_bit_alu_1_alu_output), .in1(ram_1_data), .out(out_2), .sel(Control_Unit_memtoreg));
  RAM #(.addrWidth(16), .dataWidth(16), .bus("separate")) ram_1 (
    .addr(n16_bit_alu_1_alu_output), .din(out_3), .data(ram_1_data), .str(Control_Unit_memwrite),
    .clk(CLK_out), .ld(Control_Unit_memread));  // open: sel, clr

  assign out_6[1:0] = out_5;

  // Notes on the sheet:
  //   ISA
  //   Opcode
  //   0000 ==> AND
  //   0001==>OR
  //   0010==>ADD
  //   0110==>SUB
  //   OpCode
  //   contents of rom_1 (hex, n*v repeats v):
  //   2000 2501 6082 510 8002 5082
  //   RegDst
endmodule
