// Logisim project Jump.circ as structural Verilog: 2 circuits, main circuit main
module main (
);

  Jump jump_1 ();  // open: PC, Instruction, out_3
endmodule

module Jump (
  input  [15:0] PC,
  input  [15:0] Instruction,
  output [15:0] out_3
);


  assign out_3 = {PC[15:13], Instruction[12:0]};
endmodule
