// Logisim project project 331.circ as structural Verilog: 1 circuit, main circuit main
module main (
  input  a0,
  input  b0,
  input  [2:0] OPCODE,
  input  a1,
  input  b1,
  output o0,
  output o1,
  output Sum_Carry,
  output Borrow_Carry
);

  wire adder_1_cout, adder_1_out, adder_2_out, and_1_out, and_2_out, multiplexer_1_out, multiplexer_2_out,
       multiplexer_3_out, multiplexer_4_out, not_1_out, not_2_out, or_1_out, or_2_out, subtractor_1_bout,
       subtractor_1_out, subtractor_2_out, xor_1_out, xor_2_out;

  Adder #(.width(1)) adder_1 (.a(a0), .b(b0), .out(adder_1_out), .cout(adder_1_cout));  // open: cin
  Adder #(.width(1)) adder_2 (.a(a1), .b(b1), .out(adder_2_out), .cin(adder_1_cout), .cout(Sum_Carry));
  Subtractor #(.width(1)) subtractor_1 (.a(a0), .b(b0), .out(subtractor_1_out), .bout(subtractor_1_bout));  // open: bin
  Subtractor #(.width(1)) subtractor_2 (
    .a(a1), .b(b1), .out(subtractor_2_out), .bin(subtractor_1_bout), .bout(Borrow_Carry));
  not not_1 (not_1_out, a0);
  and and_1 (and_1_out, a0, b0);
  or or_1 (or_1_out, a0, b0);
  xor xor_1 (xor_1_out, a0, b0);
  not not_2 (not_2_out, a1);
  and and_2 (and_2_out, a1, b1);
  or or_2 (or_2_out, a1, b1);
  xor xor_2 (xor_2_out, a1, b1);
  Multiplexer #(.select(2), .enable("false")) multiplexer_1 (
    .in0(not_1_out), .in1(and_1_out), .in2(or_1_out), .in3(xor_1_out), .out(multiplexer_1_out),
    .sel(OPCODE[1:0]));
  Multiplexer #(.select(2), .enable("false")) multiplexer_2 (
    .in0(not_2_out), .in1(and_2_out), .in2(or_2_out), .in3(xor_2_out), .out(multiplexer_2_out),
    .sel(OPCODE[1:0]));
  Multiplexer #(.select(2), .enable("false")) multiplexer_3 (
    .in0(adder_1_out), .in1(subtractor_1_out), .out(multiplexer_3_out), .sel(OPCODE[1:0]));  // open: in2, in3
  Multiplexer #(.select(2), .enable("false")) multiplexer_4 (
    .in0(adder_2_out), .in1(subtractor_2_out), .out(multiplexer_4_out), .sel(OPCODE[1:0]));  // open: in2, in3
  Multiplexer #(.enable("false")) multiplexer_5 (
    .in0(multiplexer_1_out), .in1(multiplexer_3_out), .out(o0), .sel(OPCODE[2]));
  Multiplexer #(.enable("false")) multiplexer_6 (
    .in0(multiplexer_2_out), .in1(multiplexer_4_out), .out(o1), .sel(OPCODE[2]));

  // Notes on the sheet:
  //   Opcodes : 
  //   Not : 000
  //   AND:001
  //   OR:010
  //   XOR:011
  //   ADD:100
  //   SUB:101
  //   MULT:110
  //   Compare:111
endmodule
